# Fritzing sketch ProyectoEducaContConex (saved by Fritzing 0.9.3b)

parts:
  Part1 = MQ-7 breakout
  Display1 = LCD screen 16x2 IIC [part_number=101290]
  DHT1 = DHT11 Humitidy and Temperature Sensor
  Part2 = MQ-3 breakout
  Part3 = Adafruit HUZZAH32 ESP32 Feather [part_number="Adafruit #3405"]
  J1 = Screw terminal - 2 pins [package=THT]

nets:
  N1: Part1.AO, Part3.A1_DAC1
  GND: Display1.GND, Part3.GND
  N2: Display1.VCC, Part3.VBUS
  N3: Display1.SDA, Part3.SCL
  N4: Display1.SCL, Part3.SDA
  N5: DHT1.VDD, J1.pin1
  N6: DHT1.DATA, DHT1.NULL, Part3.A0_DAC2
  N7: DHT1.GND, J1.pin2
  N8: Part2.AO, Part3.A2_I34

custom parts:
  MQ-7 breakout: SKU: 101282
  LCD screen 16x2 IIC: LCD screen with HD44780 controller enables showing text, symbols, value or anything else that comes from Croduino/Arduino. It is capable of showing 16 symbols in two lines and therefore can be used in many projects that need to send clearly visible and legible output information.. • Color of symbols: White • Backlight: Blue • Dimensions: 80 x 36 x 12 mm • Screen dimensions: 64.5 x 16 mm •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
  DHT11 Humitidy and Temperature Sensor: DHT11 Humidity and Temperature Sensor
  MQ-3 breakout: Alcohol sensor is capable of detecting alcohol (ethanol) particles on itself and gives the information in digital form back to us to manipulate with it. SKU:101251 • Voltage: 5V DC • Power: max 750mW • Measurement range: 0.04-4mg/L
